// Logisim project crazycpu.circ as structural Verilog: 3 circuits, main circuit main
module main (
);

  wire Aload, and_1_out, Asel, Bload, Cin, clock_1_out, clock_2_out, clock_3_out, clock_4_out, clock_5_out,
       not_1_out, not_2_out, not_3_out, not_4_out, not_5_out, not_6_out, not_7_out, PCincr, RAMwrite;
  wire [2:0] ALUop;
  wire [3:0] Aout, Bout, multiplexer_1_out, NZVC, ram_1_data, rom_3_data;
  wire [3:1] Flags_q;
  wire [7:0] Address, PC_q;

  not not_1 (not_1_out, PCincr);
  Clock clock_1 (.out(clock_1_out));
  // Probe on NZVC
  Clock clock_2 (.out(clock_2_out));
  not not_2 (not_2_out, RAMwrite);
  RAM #(.dataWidth(4)) ram_1 (
    .addr(Address), .data(ram_1_data), .sel(1'b1), .clk(clock_3_out), .ld(RAMwrite));  // open: clr
  Clock clock_3 (.out(clock_3_out));
  Counter PC (.load(not_1_out), .D(Address), .count(PCincr), .Q(PC_q), .clk(clock_1_out));  // open: carry, clr
  Register #(.width(4)) Flags (.D(NZVC), .en(not_2_out), .Q({Flags_q, Cin}), .clk(clock_2_out));  // open: clr
  // Probe on {Flags_q, Cin}
  Multiplexer #(.width(4), .enable("false")) multiplexer_1 (
    .in0(Address[3:0]), .in1(ram_1_data), .out(multiplexer_1_out), .sel(Asel));
  not not_3 (not_3_out, Aload);
  not not_4 (not_4_out, Bload);
  // Probe on ram_1_data
  assign ram_1_data = not_5_out ? rom_3_data : 4'bz;  // Controlled_Buffer controlled_buffer_1
  not not_5 (not_5_out, RAMwrite);
  Register #(.width(4)) A (.D(multiplexer_1_out), .en(not_3_out), .Q(Aout), .clk(clock_4_out));  // open: clr
  Clock clock_4 (.out(clock_4_out));
  Register #(.width(4)) B (.D(multiplexer_1_out), .en(not_4_out), .Q(Bout), .clk(clock_5_out));  // open: clr
  Clock clock_5 (.out(clock_5_out));
  // Probe on ALUop
  ROM #(.addrWidth(12)) rom_1 (
    .addr({Flags_q, Cin, PC_q}), .data({RAMwrite, Asel, Bload, Aload, PCincr, ALUop}), .sel(1'b1));
  ROM #(.addrWidth(12)) rom_2 (.addr({Flags_q, Cin, PC_q}), .data(Address), .sel(1'b1));
  ROM #(.addrWidth(12)) rom_3 (.addr({Cin, ALUop, Aout, Bout}), .data({rom_3_data, NZVC}), .sel(1'b1));
  TTY #(.rows(25), .cols(100)) tty_1 (.data({Aout[2:0], Bout}), .clk(and_1_out));  // open: we, clr
  and and_1 (and_1_out, not_6_out, not_7_out);
  not not_6 (not_6_out, Aload);
  not not_7 (not_7_out, Bload);

  // Other names for the same wires on the sheet: Aval[3:0] = Address[3:0]

  // Notes on the sheet:
  //   Sum
  //   TOPROM
  //   BOTROM
  //   contents of rom_1 (hex, n*v repeats v):
  //   a8 3d 3d e8 d8 3c e8 d8 3c e8 d8 3c e8 d8 3c e8 d8 3c e8 d8 3c e8 d8 3c e8 d8 3c b8 d8 a8 88 d8 88
  //   d8 88 d8 88 d8 88 d8 88 d8 88 d8 88 a8 3d d8 a8 88 e8 3d e8 3d e8 3d e8 3d e8 3d e8 3d e8 3d e8 3d
  //   e8 3d e8 3d e8 3d e8 3d e8 3d e8 3d e8 3d e8 3d b0 a8 3d 3d a8 5*3d a8 3d 3d a8 3d a8 3d a8 3d a8 3d
  //   e8 3d b8 e8 3d b0 e8 3d 3d e8 d8 39 e8 d8 39 e8 3d b8 e8 3d b0 e8 3d 3d e8 d8 38 e8 d8 38 3d a8 d8
  //   38 a8 d8 38 e8 d8 88 3d e8 d8 39 e8 d8 39 b0 e8 d8 88 e8 d8 88 b0 98*0 a8 3d 3d e8 d8 3c e8 d8 3c e8
  //   d8 3c e8 d8 3c e8 d8 3c e8 d8 3c e8 d8 3c e8 d8 3c b0 d8 a8 88 d8 88 d8 88 d8 88 d8 88 d8 88 d8 88
  //   d8 88 a8 3d d8 a8 88 e8 3d e8 3d e8 3d e8 3d e8 3d e8 3d e8 3d e8 3d e8 3d e8 3d e8 3d e8 3d e8 3d
  //   e8 3d e8 3d e8 3d b0 a8 3d 3d a8 5*3d a8 3d 3d a8 3d a8 3d a8 3d a8 3d e8 3d b8 e8 3d b0 e8 3d 3d e8
  //   d8 39 e8 d8 39 e8 3d b8 e8 3d b0 e8 3d 3d e8 d8 38 e8 d8 38 3d a8 d8 38 a8 d8 38 e8 d8 88 3d e8 d8
  //   39 e8 d8 39 b0 e8 d8 88 e8 d8 88 b0 98*0 a8 3d 3d e8 d8 3c e8 d8 3c e8 d8 3c e8 d8 3c e8 d8 3c e8 d8
  //   3c e8 d8 3c e8 d8 3c b8 d8 a8 88 d8 88 d8 88 d8 88 d8 88 d8 88 d8 88 d8 88 a8 3d d8 a8 88 e8 3d e8
  //   3d e8 3d e8 3d e8 3d e8 3d e8 3d e8 3d e8 3d e8 3d e8 3d e8 3d e8 3d e8 3d e8 3d e8 3d b0 a8 3d 3d
  //   a8 5*3d a8 3d 3d a8 3d a8 3d a8 3d a8 3d e8 3d b8 e8 3d b0 e8 3d 3d e8 d8 39 e8 d8 39 e8 3d b8 e8 3d
  //   b0 e8 3d 3d e8 d8 38 e8 d8 38 3d a8 d8 38 a8 d8 38 e8 d8 88 3d e8 d8 39 e8 d8 39 b0 e8 d8 88 e8 d8
  //   88 b0 98*0 a8 3d 3d e8 d8 3c e8 d8 3c e8 d8 3c e8 d8 3c e8 d8 3c e8 d8 3c e8 d8 3c e8 d8 3c b0 d8 a8
  //   88 d8 88 d8 88 d8 88 d8 88 d8 88 d8 88 d8 88 a8 3d d8 a8 88 e8 3d e8 3d e8 3d e8 3d e8 3d e8 3d e8
  //   3d e8 3d e8 3d e8 3d e8 3d e8 3d e8 3d e8 3d e8 3d e8 3d b0 a8 3d 3d a8 5*3d a8 3d 3d a8 3d a8 3d a8
  //   3d a8 3d e8 3d b8 e8 3d b0 e8 3d 3d e8 d8 39 e8 d8 39 e8 3d b8 e8 3d b0 e8 3d 3d e8 d8 38 e8 d8 38
  //   3d a8 d8 38 a8 d8 38 e8 d8 88 3d e8 d8 39 e8 d8 39 b0 e8 d8 88 e8 d8 88 b0 98*0 a8 3d 3d e8 d8 3c e8
  //   d8 3c e8 d8 3c e8 d8 3c e8 d8 3c e8 d8 3c e8 d8 3c e8 d8 3c b8 d8 a8 88 d8 88 d8 88 d8 88 d8 88 d8
  //   88 d8 88 d8 88 a8 3d d8 a8 88 e8 3d e8 3d e8 3d e8 3d e8 3d e8 3d e8 3d e8 3d e8 3d e8 3d e8 3d e8
  //   3d e8 3d e8 3d e8 3d e8 3d b0 a8 3d 3d a8 5*3d a8 3d 3d a8 3d a8 3d a8 3d a8 3d e8 3d b8 e8 3d b0 e8
  //   3d 3d e8 d8 39 e8 d8 39 e8 3d b8 e8 3d b0 e8 3d 3d e8 d8 38 e8 d8 38 3d a8 d8 38 a8 d8 38 e8 d8 88
  //   3d e8 d8 39 e8 d8 39 b8 e8 d8 88 e8 d8 88 b0 98*0 a8 3d 3d e8 d8 3c e8 d8 3c e8 d8 3c e8 d8 3c e8 d8
  //   3c e8 d8 3c e8 d8 3c e8 d8 3c b0 d8 a8 88 d8 88 d8 88 d8 88 d8 88 d8 88 d8 88 d8 88 a8 3d d8 a8 88
  //   e8 3d e8 3d e8 3d e8 3d e8 3d e8 3d e8 3d e8 3d e8 3d e8 3d e8 3d e8 3d e8 3d e8 3d e8 3d e8 3d b0
  //   a8 3d 3d a8 5*3d a8 3d 3d a8 3d a8 3d a8 3d a8 3d e8 3d b8 e8 3d b0 e8 3d 3d e8 d8 39 e8 d8 39 e8 3d
  //   b8 e8 3d b0 e8 3d 3d e8 d8 38 e8 d8 38 3d a8 d8 38 a8 d8 38 e8 d8 88 3d e8 d8 39 e8 d8 39 b8 e8 d8
  //   88 e8 d8 88 b0 98*0 a8 3d 3d e8 d8 3c e8 d8 3c e8 d8 3c e8 d8 3c e8 d8 3c e8 d8 3c e8 d8 3c e8 d8 3c
  //   b8 d8 a8 88 d8 88 d8 88 d8 88 d8 88 d8 88 d8 88 d8 88 a8 3d d8 a8 88 e8 3d e8 3d e8 3d e8 3d e8 3d
  //   e8 3d e8 3d e8 3d e8 3d e8 3d e8 3d e8 3d e8 3d e8 3d e8 3d e8 3d b0 a8 3d 3d a8 5*3d a8 3d 3d a8 3d
  //   a8 3d a8 3d a8 3d e8 3d b8 e8 3d b0 e8 3d 3d e8 d8 39 e8 d8 39 e8 3d b8 e8 3d b0 e8 3d 3d e8 d8 38
  //   e8 d8 38 3d a8 d8 38 a8 d8 38 e8 d8 88 3d e8 d8 39 e8 d8 39 b8 e8 d8 88 e8 d8 88 b0 98*0 a8 3d 3d e8
  //   d8 3c e8 d8 3c e8 d8 3c e8 d8 3c e8 d8 3c e8 d8 3c e8 d8 3c e8 d8 3c b0 d8 a8 88 d8 88 d8 88 d8 88
  //   d8 88 d8 88 d8 88 d8 88 a8 3d d8 a8 88 e8 3d e8 3d e8 3d e8 3d e8 3d e8 3d e8 3d e8 3d e8 3d e8 3d
  //   e8 3d e8 3d e8 3d e8 3d e8 3d e8 3d b0 a8 3d 3d a8 5*3d a8 3d 3d a8 3d a8 3d a8 3d a8 3d e8 3d b8 e8
  //   3d b0 e8 3d 3d e8 d8 39 e8 d8 39 e8 3d b8 e8 3d b0 e8 3d 3d e8 d8 38 e8 d8 38 3d a8 d8 38 a8 d8 38
  //   e8 d8 88 3d e8 d8 39 e8 d8 39 b8 e8 d8 88 e8 d8 88 b0 98*0 a8 3d 3d e8 d8 3c e8 d8 3c e8 d8 3c e8 d8
  //   3c e8 d8 3c e8 d8 3c e8 d8 3c e8 d8 3c b8 d8 a8 88 d8 88 d8 88 d8 88 d8 88 d8 88 d8 88 d8 88 a8 3d
  //   d8 a8 88 e8 3d e8 3d e8 3d e8 3d e8 3d e8 3d e8 3d e8 3d e8 3d e8 3d e8 3d e8 3d e8 3d e8 3d e8 3d
  //   e8 3d b0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
  //   contents of rom_2 (hex, n*v repeats v):
  //   1 8 10 8 10 18 7 f 17 6 e 16 5 d 15 4 c 14 3 b 13 2 a 12 1 9 11 0 11 3 3 12 3 13 3 14 3 15 3 16 3 17
  //   3 18 3 a ff ff 0 0 10 8 18 10 f 7 17 f e 6 16 e d 5 15 d c 4 14 c b 3 13 b a 2 12 a 9 1 11 9 3 2 8 a
  //   0 c 9 e 2 3 a b d f f 1 10 3 0 6 1 0 4 0 e 5 6f f 5 ff 3 4 3 2 5 2 2 4 0 e 5 7e f 5 ff 1 4 1 0 5 0
  //   ff b 1 7 3 0 6 8 9 ff ff 7 10 7 6 e 6 8c a b ff c d ff 67 98*0 1 8 10 8 10 18 7 f 17 6 e 16 5 d 15 4
  //   c 14 3 b 13 2 a 12 1 9 11 53 11 3 3 12 3 13 3 14 3 15 3 16 3 17 3 18 3 a ff ff 0 0 10 8 18 10 f 7 17
  //   f e 6 16 e d 5 15 d c 4 14 c b 3 13 b a 2 12 a 9 1 11 9 3 2 8 a 0 c 9 e 2 3 a b d f f 1 10 3 0 6 1 0
  //   4 0 e 5 6f f 5 ff 3 4 3 2 5 2 2 4 0 e 5 7e f 5 ff 1 4 1 0 5 0 ff b 1 7 3 0 6 8 9 ff ff 7 10 7 6 e 6
  //   8c a b ff c d ff 67 98*0 1 8 10 8 10 18 7 f 17 6 e 16 5 d 15 4 c 14 3 b 13 2 a 12 1 9 11 0 11 3 3 12
  //   3 13 3 14 3 15 3 16 3 17 3 18 3 a ff ff 0 0 10 8 18 10 f 7 17 f e 6 16 e d 5 15 d c 4 14 c b 3 13 b
  //   a 2 12 a 9 1 11 9 3 2 8 a 0 c 9 e 2 3 a b d f f 1 10 3 0 6 1 0 4 0 e 5 6f f 5 ff 3 4 3 2 5 2 2 4 0 e
  //   5 7e f 5 ff 1 4 1 0 5 0 ff b 1 7 3 0 6 8 9 ff ff 7 10 7 6 e 6 8c a b ff c d ff 67 98*0 1 8 10 8 10
  //   18 7 f 17 6 e 16 5 d 15 4 c 14 3 b 13 2 a 12 1 9 11 53 11 3 3 12 3 13 3 14 3 15 3 16 3 17 3 18 3 a
  //   ff ff 0 0 10 8 18 10 f 7 17 f e 6 16 e d 5 15 d c 4 14 c b 3 13 b a 2 12 a 9 1 11 9 3 2 8 a 0 c 9 e
  //   2 3 a b d f f 1 10 3 0 6 1 0 4 0 e 5 6f f 5 ff 3 4 3 2 5 2 2 4 0 e 5 7e f 5 ff 1 4 1 0 5 0 ff b 1 7
  //   3 0 6 8 9 ff ff 7 10 7 6 e 6 8c a b ff c d ff 67 98*0 1 8 10 8 10 18 7 f 17 6 e 16 5 d 15 4 c 14 3 b
  //   13 2 a 12 1 9 11 0 11 3 3 12 3 13 3 14 3 15 3 16 3 17 3 18 3 a ff ff 0 0 10 8 18 10 f 7 17 f e 6 16
  //   e d 5 15 d c 4 14 c b 3 13 b a 2 12 a 9 1 11 9 3 2 8 a 0 c 9 e 2 3 a b d f f 1 10 3 0 6 1 0 4 0 e 5
  //   6f f 5 ff 3 4 3 2 5 2 2 4 0 e 5 7e f 5 ff 1 4 1 0 5 0 ff b 1 7 3 0 6 8 9 ff ff 7 10 7 6 e 6 0 a b ff
  //   c d ff 67 98*0 1 8 10 8 10 18 7 f 17 6 e 16 5 d 15 4 c 14 3 b 13 2 a 12 1 9 11 53 11 3 3 12 3 13 3
  //   14 3 15 3 16 3 17 3 18 3 a ff ff 0 0 10 8 18 10 f 7 17 f e 6 16 e d 5 15 d c 4 14 c b 3 13 b a 2 12
  //   a 9 1 11 9 3 2 8 a 0 c 9 e 2 3 a b d f f 1 10 3 0 6 1 0 4 0 e 5 6f f 5 ff 3 4 3 2 5 2 2 4 0 e 5 7e f
  //   5 ff 1 4 1 0 5 0 ff b 1 7 3 0 6 8 9 ff ff 7 10 7 6 e 6 0 a b ff c d ff 67 98*0 1 8 10 8 10 18 7 f 17
  //   6 e 16 5 d 15 4 c 14 3 b 13 2 a 12 1 9 11 0 11 3 3 12 3 13 3 14 3 15 3 16 3 17 3 18 3 a ff ff 0 0 10
  //   8 18 10 f 7 17 f e 6 16 e d 5 15 d c 4 14 c b 3 13 b a 2 12 a 9 1 11 9 3 2 8 a 0 c 9 e 2 3 a b d f f
  //   1 10 3 0 6 1 0 4 0 e 5 6f f 5 ff 3 4 3 2 5 2 2 4 0 e 5 7e f 5 ff 1 4 1 0 5 0 ff b 1 7 3 0 6 8 9 ff
  //   ff 7 10 7 6 e 6 0 a b ff c d ff 67 98*0 1 8 10 8 10 18 7 f 17 6 e 16 5 d 15 4 c 14 3 b 13 2 a 12 1 9
  //   11 53 11 3 3 12 3 13 3 14 3 15 3 16 3 17 3 18 3 a ff ff 0 0 10 8 18 10 f 7 17 f e 6 16 e d 5 15 d c
  //   4 14 c b 3 13 b a 2 12 a 9 1 11 9 3 2 8 a 0 c 9 e 2 3 a b d f f 1 10 3 0 6 1 0 4 0 e 5 6f f 5 ff 3 4
  //   3 2 5 2 2 4 0 e 5 7e f 5 ff 1 4 1 0 5 0 ff b 1 7 3 0 6 8 9 ff ff 7 10 7 6 e 6 0 a b ff c d ff 67
  //   98*0 1 8 10 8 10 18 7 f 17 6 e 16 5 d 15 4 c 14 3 b 13 2 a 12 1 9 11 0 11 3 3 12 3 13 3 14 3 15 3 16
  //   3 17 3 18 3 a ff ff 0 0 10 8 18 10 f 7 17 f e 6 16 e d 5 15 d c 4 14 c b 3 13 b a 2 12 a 9 1 11 9 3
  //   2 8 a 0 c 9 e 2 3 a b d f f 1 10 3 0 6 1 0 4 6d e 5 6f f 5 ff 3 4 3 2 5 2 2 4 7c e 5 7e f 5 ff 1 4 1
  //   0 5 0 ff b 1 7 3 0 6 8 9 ff ff 7 10 7 6 e 6 8c a b ff c d ff 67 98*0 1 8 10 8 10 18 7 f 17 6 e 16 5
  //   d 15 4 c 14 3 b 13 2 a 12 1 9 11 53 11 3 3 12 3 13 3 14 3 15 3 16 3 17 3 18 3 a ff ff 0 0 10 8 18 10
  //   f 7 17 f e 6 16 e d 5 15 d c 4 14 c b 3 13 b a 2 12 a 9 1 11 9 3 2 8 a 0 c 9 e 2 3 a b d f f 1 10 3
  //   0 6 1 0 4 6d e 5 6f f 5 ff 3 4 3 2 5 2 2 4 7c e 5 7e f 5 ff 1 4 1 0 5 0 ff b 1 7 3 0 6 8 9 ff ff 7
  //   10 7 6 e 6 8c a b ff c d ff 67 98*0 1 8 10 8 10 18 7 f 17 6 e 16 5 d 15 4 c 14 3 b 13 2 a 12 1 9 11
  //   0 11 3 3 12 3 13 3 14 3 15 3 16 3 17 3 18 3 a ff ff 0 0 10 8 18 10 f 7 17 f e 6 16 e d 5 15 d c 4 14
  //   c b 3 13 b a 2 12 a 9 1 11 9 3 2 8 a 0 c 9 e 2 3 a b d f f 1 10 3 0 6 1 0 4 6d e 5 6f f 5 ff 3 4 3 2
  //   5 2 2 4 7c e 5 7e f 5 ff 1 4 1 0 5 0 ff b 1 7 3 0 6 8 9 ff ff 7 10 7 6 e 6 8c a b ff c d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
  //   ALUROM
  //   contents of rom_3 (hex, n*v repeats v):
  //   4 10 20 30 40 50 60 70 88 98 a8 b8 c8 d8 e8 f8 10 20 30 40 50 60 70 8a 98 a8 b8 c8 d8 e8 f8 5 20 30
  //   40 50 60 70 8a 9a a8 b8 c8 d8 e8 f8 5 11 30 40 50 60 70 8a 9a aa b8 c8 d8 e8 f8 5 11 21 40 50 60 70
  //   8a 9a aa ba c8 d8 e8 f8 5 11 21 31 50 60 70 8a 9a aa ba ca d8 e8 f8 5 11 21 31 41 60 70 8a 9a aa ba
  //   ca da e8 f8 5 11 21 31 41 51 70 8a 9a aa ba ca da ea f8 5 11 21 31 41 51 61 88 98 a8 b8 c8 d8 e8 f8
  //   7 13 23 33 43 53 63 73 98 a8 b8 c8 d8 e8 f8 5 13 23 33 43 53 63 73 89 a8 b8 c8 d8 e8 f8 5 11 23 33
  //   43 53 63 73 89 99 b8 c8 d8 e8 f8 5 11 21 33 43 53 63 73 89 99 a9 c8 d8 e8 f8 5 11 21 31 43 53 63 73
  //   89 99 a9 b9 d8 e8 f8 5 11 21 31 41 53 63 73 89 99 a9 b9 c9 e8 f8 5 11 21 31 41 51 63 73 89 99 a9 b9
  //   c9 d9 f8 5 11 21 31 41 51 61 73 89 99 a9 b9 c9 d9 e9 4 fb eb db cb bb ab 9b 89 71 61 51 41 31 21 11
  //   10 4 fb eb db cb bb ab 99 89 71 61 51 41 31 21 20 10 4 fb eb db cb bb a9 99 89 71 61 51 41 31 30 20
  //   10 4 fb eb db cb b9 a9 99 89 71 61 51 41 40 30 20 10 4 fb eb db c9 b9 a9 99 89 71 61 51 50 40 30 20
  //   10 4 fb eb d9 c9 b9 a9 99 89 71 61 60 50 40 30 20 10 4 fb e9 d9 c9 b9 a9 99 89 71 70 60 50 40 30 20
  //   10 4 f9 e9 d9 c9 b9 a9 99 89 88 70 60 50 40 30 20 10 6 f9 e9 d9 c9 b9 a9 99 98 88 70 60 50 40 30 20
  //   12 6 f9 e9 d9 c9 b9 a9 a8 98 88 70 60 50 40 30 22 12 6 f9 e9 d9 c9 b9 b8 a8 98 88 70 60 50 40 32 22
  //   12 6 f9 e9 d9 c9 c8 b8 a8 98 88 70 60 50 42 32 22 12 6 f9 e9 d9 d8 c8 b8 a8 98 88 70 60 52 42 32 22
  //   12 6 f9 e9 e8 d8 c8 b8 a8 98 88 70 62 52 42 32 22 12 6 f9 f8 e8 d8 c8 b8 a8 98 88 72 62 52 42 32 22
  //   12 6 17*4 10 4 10 4 10 4 10 4 10 4 10 4 10 4 10 4 4 20 20 4 4 20 20 4 4 20 20 4 4 20 20 4 10 20 30 4
  //   10 20 30 4 10 20 30 4 10 20 30 4*4 4*40 4*4 4*40 4 10 4 10 40 50 40 50 4 10 4 10 40 50 40 50 4 4 20
  //   20 40 40 60 60 4 4 20 20 40 40 60 60 4 10 20 30 40 50 60 70 4 10 20 30 40 50 60 70 8*4 8*88 4 10 4
  //   10 4 10 4 10 88 98 88 98 88 98 88 98 4 4 20 20 4 4 20 20 88 88 a8 a8 88 88 a8 a8 4 10 20 30 4 10 20
  //   30 88 98 a8 b8 88 98 a8 b8 4*4 4*40 4*88 4*c8 4 10 4 10 40 50 40 50 88 98 88 98 c8 d8 c8 d8 4 4 20
  //   20 40 40 60 60 88 88 a8 a8 c8 c8 e8 e8 4 10 20 30 40 50 60 70 88 98 a8 b8 c8 d8 e8 f8 4 10 20 30 40
  //   50 60 70 88 98 a8 b8 c8 d8 e8 f8 10 10 30 30 50 50 70 70 98 98 b8 b8 d8 d8 f8 f8 20 30 20 30 60 70
  //   60 70 a8 b8 a8 b8 e8 f8 e8 f8 4*30 4*70 4*b8 4*f8 40 50 60 70 40 50 60 70 c8 d8 e8 f8 c8 d8 e8 f8 50
  //   50 70 70 50 50 70 70 d8 d8 f8 f8 d8 d8 f8 f8 60 70 60 70 60 70 60 70 e8 f8 e8 f8 e8 f8 e8 f8 8*70
  //   8*f8 88 98 a8 b8 c8 d8 e8 f8 88 98 a8 b8 c8 d8 e8 f8 98 98 b8 b8 d8 d8 f8 f8 98 98 b8 b8 d8 d8 f8 f8
  //   a8 b8 a8 b8 e8 f8 e8 f8 a8 b8 a8 b8 e8 f8 e8 f8 4*b8 4*f8 4*b8 4*f8 c8 d8 e8 f8 c8 d8 e8 f8 c8 d8 e8
  //   f8 c8 d8 e8 f8 d8 d8 f8 f8 d8 d8 f8 f8 d8 d8 f8 f8 d8 d8 f8 f8 e8 f8 e8 f8 e8 f8 e8 f8 e8 f8 e8 f8
  //   e8 f8 e8 17*f8 4 10 20 30 40 50 60 70 80 90 5 5*4 10 20 30 40 50 60 70 80 90 5 11 5*4 20 30 40 50 60
  //   70 80 90 5 11 21 5*4 30 40 50 60 70 80 90 5 11 21 31 5*4 40 50 60 70 80 90 5 11 21 31 41 5*4 50 60
  //   70 80 90 5 11 21 31 41 51 5*4 60 70 80 90 5 11 21 31 41 51 61 5*4 70 80 90 5 11 21 31 41 51 61 71
  //   5*4 80 90 5 11 21 31 41 51 61 71 81 5*4 90 5 11 21 31 41 51 61 71 81 91 5*4 5 11 21 31 41 51 61 71
  //   81 91 a1 101*4 16*10 16*20 16*30 16*40 16*50 16*60 16*70 16*88 16*98 16*a8 16*b8 16*c8 16*d8 16*e8
  //   16*f8 4 10 20 30 40 50 60 70 88 98 a8 b8 c8 d8 e8 f8 4 10 20 30 40 50 60 70 88 98 a8 b8 c8 d8 e8 f8
  //   4 10 20 30 40 50 60 70 88 98 a8 b8 c8 d8 e8 f8 4 10 20 30 40 50 60 70 88 98 a8 b8 c8 d8 e8 f8 4 10
  //   20 30 40 50 60 70 88 98 a8 b8 c8 d8 e8 f8 4 10 20 30 40 50 60 70 88 98 a8 b8 c8 d8 e8 f8 4 10 20 30
  //   40 50 60 70 88 98 a8 b8 c8 d8 e8 f8 4 10 20 30 40 50 60 70 88 98 a8 b8 c8 d8 e8 f8 4 10 20 30 40 50
  //   60 70 88 98 a8 b8 c8 d8 e8 f8 4 10 20 30 40 50 60 70 88 98 a8 b8 c8 d8 e8 f8 4 10 20 30 40 50 60 70
  //   88 98 a8 b8 c8 d8 e8 f8 4 10 20 30 40 50 60 70 88 98 a8 b8 c8 d8 e8 f8 4 10 20 30 40 50 60 70 88 98
  //   a8 b8 c8 d8 e8 f8 4 10 20 30 40 50 60 70 88 98 a8 b8 c8 d8 e8 f8 4 10 20 30 40 50 60 70 88 98 a8 b8
  //   c8 d8 e8 f8 4 10 20 30 40 50 60 70 88 98 a8 b8 c8 d8 e8 f8 16*10 16*20 16*30 16*40 16*50 16*60 16*70
  //   8*8a 8*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
endmodule

module ALU (
  input  [2:0] Op,
  input  FlagWr,
  input  [7:0] Arg1,
  input  Clk,
  input  [7:0] Arg2,
  output [3:0] NZVC,
  output [7:0] Output
);

  wire Coutlow, Noutlow, Voutlow, Zoutlow;
  wire [7:4] rom_1_data;

  ROM #(.addrWidth(13)) rom_1 (
    .addr({Op, Arg1[7:4], Arg2[7:4], Zoutlow, Coutlow}), .data({rom_1_data, Output[7:4]}));  // open: sel
  ROM #(.addrWidth(13)) rom_2 (
    .addr({Op, Arg1[3:0], Arg2[3:0], 2'b10}), .data({Noutlow, Zoutlow, Voutlow, Coutlow, Output[3:0]}));  // open: sel
  Register #(.width(4)) Flags (.D(rom_1_data), .en(FlagWr), .Q(NZVC), .clk(Clk));  // open: clr

  // Other names for the same wires on the sheet: Arg2high[3:0] = Arg2[7:4]; Arg1high[3:0] = Arg1[7:4];
  //   Arg2low[3:0] = Arg2[3:0]; Arg1low[3:0] = Arg1[3:0]; ALUop[2:0] = Op; Resultlow[3:0] = Output[3:0]

  // Notes on the sheet:
  //   contents of rom_1 (hex, n*v repeats v):
  //   0 1 40 1 1 2 1 2 2 3 2 3 3 4 3 4 4 5 4 5 5 6 5 6 6 7 6 7 7 a8 7 a8 88 89 88 89 89 8a 89 8a 8a 8b 8a
  //   8b 8b 8c 8b 8c 8c 8d 8c 8d 8d 8e 8d 8e 8e 8f 8e 8f 8f 10 8f 50 1 2 1 2 2 3 2 3 3 4 3 4 4 5 4 5 5 6 5
  //   6 6 7 6 7 7 a8 7 a8 a8 a9 a8 a9 89 8a 89 8a 8a 8b 8a 8b 8b 8c 8b 8c 8c 8d 8c 8d 8d 8e 8d 8e 8e 8f 8e
  //   8f 8f 10 8f 50 10 11 50 11 2 3 2 3 3 4 3 4 4 5 4 5 5 6 5 6 6 7 6 7 7 a8 7 a8 a8 a9 a8 a9 a9 aa a9 aa
  //   8a 8b 8a 8b 8b 8c 8b 8c 8c 8d 8c 8d 8d 8e 8d 8e 8e 8f 8e 8f 8f 10 8f 50 10 11 50 11 11 12 11 12 3 4
  //   3 4 4 5 4 5 5 6 5 6 6 7 6 7 7 a8 7 a8 a8 a9 a8 a9 a9 aa a9 aa aa ab aa ab 8b 8c 8b 8c 8c 8d 8c 8d 8d
  //   8e 8d 8e 8e 8f 8e 8f 8f 10 8f 50 10 11 50 11 11 12 11 12 12 13 12 13 4 5 4 5 5 6 5 6 6 7 6 7 7 a8 7
  //   a8 a8 a9 a8 a9 a9 aa a9 aa aa ab aa ab ab ac ab ac 8c 8d 8c 8d 8d 8e 8d 8e 8e 8f 8e 8f 8f 10 8f 50
  //   10 11 50 11 11 12 11 12 12 13 12 13 13 14 13 14 5 6 5 6 6 7 6 7 7 a8 7 a8 a8 a9 a8 a9 a9 aa a9 aa aa
  //   ab aa ab ab ac ab ac ac ad ac ad 8d 8e 8d 8e 8e 8f 8e 8f 8f 10 8f 50 10 11 50 11 11 12 11 12 12 13
  //   12 13 13 14 13 14 14 15 14 15 6 7 6 7 7 a8 7 a8 a8 a9 a8 a9 a9 aa a9 aa aa ab aa ab ab ac ab ac ac
  //   ad ac ad ad ae ad ae 8e 8f 8e 8f 8f 10 8f 50 10 11 50 11 11 12 11 12 12 13 12 13 13 14 13 14 14 15
  //   14 15 15 16 15 16 7 a8 7 a8 a8 a9 a8 a9 a9 aa a9 aa aa ab aa ab ab ac ab ac ac ad ac ad ad ae ad ae
  //   ae af ae af 8f 10 8f 50 10 11 50 11 11 12 11 12 12 13 12 13 13 14 13 14 14 15 14 15 15 16 15 16 16
  //   17 16 17 88 89 88 89 89 8a 89 8a 8a 8b 8a 8b 8b 8c 8b 8c 8c 8d 8c 8d 8d 8e 8d 8e 8e 8f 8e 8f 8f 10
  //   8f 50 30 31 70 31 31 32 31 32 32 33 32 33 33 34 33 34 34 35 34 35 35 36 35 36 36 37 36 37 37 98 37
  //   98 89 8a 89 8a 8a 8b 8a 8b 8b 8c 8b 8c 8c 8d 8c 8d 8d 8e 8d 8e 8e 8f 8e 8f 8f 10 8f 50 10 11 50 11
  //   31 32 31 32 32 33 32 33 33 34 33 34 34 35 34 35 35 36 35 36 36 37 36 37 37 98 37 98 98 99 98 99 8a
  //   8b 8a 8b 8b 8c 8b 8c 8c 8d 8c 8d 8d 8e 8d 8e 8e 8f 8e 8f 8f 10 8f 50 10 11 50 11 11 12 11 12 32 33
  //   32 33 33 34 33 34 34 35 34 35 35 36 35 36 36 37 36 37 37 98 37 98 98 99 98 99 99 9a 99 9a 8b 8c 8b
  //   8c 8c 8d 8c 8d 8d 8e 8d 8e 8e 8f 8e 8f 8f 10 8f 50 10 11 50 11 11 12 11 12 12 13 12 13 33 34 33 34
  //   34 35 34 35 35 36 35 36 36 37 36 37 37 98 37 98 98 99 98 99 99 9a 99 9a 9a 9b 9a 9b 8c 8d 8c 8d 8d
  //   8e 8d 8e 8e 8f 8e 8f 8f 10 8f 50 10 11 50 11 11 12 11 12 12 13 12 13 13 14 13 14 34 35 34 35 35 36
  //   35 36 36 37 36 37 37 98 37 98 98 99 98 99 99 9a 99 9a 9a 9b 9a 9b 9b 9c 9b 9c 8d 8e 8d 8e 8e 8f 8e
  //   8f 8f 10 8f 50 10 11 50 11 11 12 11 12 12 13 12 13 13 14 13 14 14 15 14 15 35 36 35 36 36 37 36 37
  //   37 98 37 98 98 99 98 99 99 9a 99 9a 9a 9b 9a 9b 9b 9c 9b 9c 9c 9d 9c 9d 8e 8f 8e 8f 8f 10 8f 50 10
  //   11 50 11 11 12 11 12 12 13 12 13 13 14 13 14 14 15 14 15 15 16 15 16 36 37 36 37 37 98 37 98 98 99
  //   98 99 99 9a 99 9a 9a 9b 9a 9b 9b 9c 9b 9c 9c 9d 9c 9d 9d 9e 9d 9e 8f 10 8f 50 10 11 50 11 11 12 11
  //   12 12 13 12 13 13 14 13 14 14 15 14 15 15 16 15 16 16 17 16 17 37 98 37 98 98 99 98 99 99 9a 99 9a
  //   9a 9b 9a 9b 9b 9c 9b 9c 9c 9d 9c 9d 9d 9e 9d 9e 9e 9f 9e 9f 0 bf 40 bf bf be bf be be bd be bd bd bc
  //   bd bc bc bb bc bb bb ba bb ba ba b9 ba b9 b9 b8 b9 b8 98 17 98 17 17 16 17 16 16 15 16 15 15 14 15
  //   14 14 13 14 13 13 12 13 12 12 11 12 11 11 10 11 50 1 0 1 40 0 bf 40 bf bf be bf be be bd be bd bd bc
  //   bd bc bc bb bc bb bb ba bb ba ba b9 ba b9 99 98 99 98 98 17 98 17 17 16 17 16 16 15 16 15 15 14 15
  //   14 14 13 14 13 13 12 13 12 12 11 12 11 2 1 2 1 1 0 1 40 0 bf 40 bf bf be bf be be bd be bd bd bc bd
  //   bc bc bb bc bb bb ba bb ba 9a 99 9a 99 99 98 99 98 98 17 98 17 17 16 17 16 16 15 16 15 15 14 15 14
  //   14 13 14 13 13 12 13 12 3 2 3 2 2 1 2 1 1 0 1 40 0 bf 40 bf bf be bf be be bd be bd bd bc bd bc bc
  //   bb bc bb 9b 9a 9b 9a 9a 99 9a 99 99 98 99 98 98 17 98 17 17 16 17 16 16 15 16 15 15 14 15 14 14 13
  //   14 13 4 3 4 3 3 2 3 2 2 1 2 1 1 0 1 40 0 bf 40 bf bf be bf be be bd be bd bd bc bd bc 9c 9b 9c 9b 9b
  //   9a 9b 9a 9a 99 9a 99 99 98 99 98 98 17 98 17 17 16 17 16 16 15 16 15 15 14 15 14 5 4 5 4 4 3 4 3 3 2
  //   3 2 2 1 2 1 1 0 1 40 0 bf 40 bf bf be bf be be bd be bd 9d 9c 9d 9c 9c 9b 9c 9b 9b 9a 9b 9a 9a 99 9a
  //   99 99 98 99 98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
  //   contents of rom_2 (hex, n*v repeats v):
  //   0 1 40 1 1 2 1 2 2 3 2 3 3 4 3 4 4 5 4 5 5 6 5 6 6 7 6 7 7 a8 7 a8 88 89 88 89 89 8a 89 8a 8a 8b 8a
  //   8b 8b 8c 8b 8c 8c 8d 8c 8d 8d 8e 8d 8e 8e 8f 8e 8f 8f 10 8f 50 1 2 1 2 2 3 2 3 3 4 3 4 4 5 4 5 5 6 5
  //   6 6 7 6 7 7 a8 7 a8 a8 a9 a8 a9 89 8a 89 8a 8a 8b 8a 8b 8b 8c 8b 8c 8c 8d 8c 8d 8d 8e 8d 8e 8e 8f 8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
  //   (unused)
  //   (unused)
endmodule

module Control (
  input  [3:0] NZVC,
  input  [7:0] Opcode,
  output IDXchoice,
  output [1:0] PARop,
  output [1:0] Stkop,
  output [7:0] Awriters,
  output Clk,
  output [1:0] PCop,
  output [7:0] Dreaders,
  output [7:0] Dwriters
);

  wire [2:0] Phase_q, rom_1_data;
  wire [5:0] rom_2_data;

  Counter #(.width(3), .max('h7)) Phase (
    .count(1'b1), .Q(Phase_q), .clk(Clk), .clr(Dwriters[7]));  // open: load, D, carry
  Clock clock_1 (.out(Clk));
  // Probe on Phase_q
  ROM #(.addrWidth(13)) rom_1 (
    .addr({NZVC, Phase_q, Opcode[5:0]}), .data({IDXchoice, PARop, Stkop, rom_1_data}));  // open: sel
  ROM #(.addrWidth(13)) rom_2 (.addr({NZVC, Phase_q, Opcode[5:0]}), .data({PCop, rom_2_data}));  // open: sel
  Demultiplexer #(.select(3), .enable("false")) demultiplexer_1 (
    .out0(Awriters[0]), .out1(Awriters[1]), .out2(Awriters[2]), .out3(Awriters[3]), .out4(Awriters[4]),
    .out5(Awriters[5]), .out6(Awriters[6]), .out7(Awriters[7]), .in(1'b1), .sel(rom_1_data));
  Demultiplexer #(.select(3), .enable("false")) demultiplexer_2 (
    .out0(Dreaders[0]), .out1(Dreaders[1]), .out2(Dreaders[2]), .out3(Dreaders[3]), .out4(Dreaders[4]),
    .out5(Dreaders[5]), .out6(Dreaders[6]), .out7(Dreaders[7]), .in(1'b1), .sel(rom_2_data[5:3]));
  Demultiplexer #(.select(3), .enable("false")) demultiplexer_3 (
    .out0(Dwriters[0]), .out1(Dwriters[1]), .out2(Dwriters[2]), .out3(Dwriters[3]), .out4(Dwriters[4]),
    .out5(Dwriters[5]), .out6(Dwriters[6]), .out7(Dwriters[7]), .in(1'b1), .sel(rom_2_data[2:0]));

  // Other names for the same wires on the sheet: PhaseRst = Dwriters[7]

  // Notes on the sheet:
  //   contents of rom_1 (hex, n*v repeats v):
  //   107*0 8 9*0 1b 1b 6*0 8 8 44*0 b 0 0 82 14*0 3 3 6*0 1 10*0 7*1 0 0 1 1 0 1 1 1 0 0 1 1 4*0 2 11 41
  //   1b 3 41 2 0 1 7*0 41 49*0 24 1b 1 24 0 0 1 7*0 24 49*0 4 1 0 4 10*0 4 49*0 1 0 0 1 10*0 2 179*0 8
  //   9*0 1b 1b 6*0 8 8 44*0 b 0 0 82 14*0 3 3 6*0 1 10*0 7*1 0 0 1 1 0 4*1 0 0 1 4*0 2 11 41 1b 3 41 2 0
  //   1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
  //   contents of rom_2 (hex, n*v repeats v):
  //   48*6a 5*0 6a 6a 6a 5*0 6a 6a 0 5*9 5a 9 7*11 4a 52 19*5a b 13 39 39 4*5a 0 5a 5a 52 5a 5*0 31 31 5a
  //   8*0 5*7 62 10*7 19*62 4*7 4*62 1a 62 62 a 62 5*0 7 7 62 5*0 a 12 6*0 80 10*0 5*31 a 12 0 0 80 80 0
  //   80 31 31 0 0 80 80 4*0 a 0 0 35 22 0 31 7 12 13*0 7 7 6*0 7 15*0 14*7 4*0 7 7 1a 34 80 1a 7 0 31 7*0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
endmodule
